// Logisim project Etch-a-Sketch.circ as structural Verilog: 6 circuits, main circuit main
module main (
);

  wire not_1_out, not_2_out, or_1_out, p, Res;
  wire [4:0] C5;
  wire [5:0] Con_1, Con_2, counter_2_count_6, Pinout;
  wire [31:0] buffer_1_out, buffer_8_out, buffer_15_out, buffer_64_out, buffer_69_out, horizctrl_1_out1_2,
       LY, memory_1_out_1, memory_1_out_2, memory_1_out_3, memory_1_out_4, memory_1_out_5, memory_1_out_6,
       memory_1_out_7, memory_1_out_8, memory_1_out_9, memory_1_out_10, memory_1_out_11, memory_1_out_12,
       memory_1_out_13, memory_1_out_14, memory_1_out_15, memory_1_out_16, memory_1_out_17, memory_1_out_18,
       memory_1_out_19, memory_1_out_20, memory_1_out_21, memory_1_out_22, memory_1_out_23, memory_1_out_24,
       memory_1_out_25, memory_1_out_26, memory_1_out_27, memory_1_out_28, memory_1_out_29, memory_1_out_30,
       memory_1_out_31, memory_1_out_32, memory_1_out_33, memory_1_out_34, memory_1_out_35, memory_1_out_36,
       memory_1_out_37, memory_1_out_38, memory_1_out_39, memory_1_out_40, memory_1_out_41, memory_1_out_42,
       memory_1_out_43, memory_1_out_44, memory_1_out_45, memory_1_out_46, memory_1_out_47, memory_1_out_48,
       memory_1_out_49, memory_1_out_50, memory_1_out_51, memory_1_out_52, memory_1_out_53, memory_1_out_54,
       memory_1_out_55, memory_1_out_56, memory_1_out_57, memory_1_out_58, memory_1_out_59, memory_1_out_60,
       memory_1_out_61, memory_1_out_62, memory_1_out_63, memory_1_out_64, X1, X2, XL1, XL2;

  assign buffer_1_out = X1;  // Buffer buffer_1, 32 bits wide
  DotMatrix #(.matrixcols(1), .matrixrows(32)) dotmatrix_1 (.col0(LY));
  DotMatrix #(.matrixcols(32), .matrixrows(1)) dotmatrix_2 (
    .col0(buffer_1_out[31]), .col1(buffer_1_out[30]), .col2(buffer_1_out[29]), .col3(buffer_1_out[28]),
    .col4(buffer_1_out[27]), .col5(buffer_1_out[26]), .col6(buffer_1_out[25]), .col7(buffer_1_out[24]),
    .col8(buffer_1_out[23]), .col9(buffer_1_out[22]), .col10(buffer_1_out[21]), .col11(buffer_1_out[20]),
    .col12(buffer_1_out[19]), .col13(buffer_1_out[18]), .col14(buffer_1_out[17]), .col15(buffer_1_out[16]),
    .col16(buffer_1_out[15]), .col17(buffer_1_out[14]), .col18(buffer_1_out[13]), .col19(buffer_1_out[12]),
    .col20(buffer_1_out[11]), .col21(buffer_1_out[10]), .col22(buffer_1_out[9]), .col23(buffer_1_out[8]),
    .col24(buffer_1_out[7]), .col25(buffer_1_out[6]), .col26(buffer_1_out[5]), .col27(buffer_1_out[4]),
    .col28(buffer_1_out[3]), .col29(buffer_1_out[2]), .col30(buffer_1_out[1]), .col31(buffer_1_out[0]));
  DotMatrix #(.matrixcols(32), .matrixrows(32)) dotmatrix_3 (
    .col0(memory_1_out_1), .col1(memory_1_out_2), .col2(memory_1_out_3), .col3(memory_1_out_4),
    .col4(memory_1_out_5), .col5(memory_1_out_6), .col6(memory_1_out_7), .col7(memory_1_out_8),
    .col8(memory_1_out_9), .col9(memory_1_out_10), .col10(memory_1_out_11), .col11(memory_1_out_12),
    .col12(memory_1_out_13), .col13(memory_1_out_14), .col14(memory_1_out_15), .col15(memory_1_out_16),
    .col16(memory_1_out_17), .col17(memory_1_out_18), .col18(memory_1_out_19), .col19(memory_1_out_20),
    .col20(memory_1_out_21), .col21(memory_1_out_22), .col22(memory_1_out_23), .col23(memory_1_out_24),
    .col24(memory_1_out_25), .col25(memory_1_out_26), .col26(memory_1_out_27), .col27(memory_1_out_28),
    .col28(memory_1_out_29), .col29(memory_1_out_30), .col30(memory_1_out_31), .col31(memory_1_out_32));
  Memory memory_1 (
    .Clock(or_1_out), .Reset(Res), .X_Location_1(XL1), .X_Location_2(XL2), .Y_Location(LY),
    .Out_1(memory_1_out_1), .Out_2(memory_1_out_2), .Out_3(memory_1_out_3), .Out_4(memory_1_out_4),
    .Out_5(memory_1_out_5), .Out_6(memory_1_out_6), .Out_7(memory_1_out_7), .Out_8(memory_1_out_8),
    .Out_9(memory_1_out_9), .Out_10(memory_1_out_10), .Out_11(memory_1_out_11), .Out_12(memory_1_out_12),
    .Out_13(memory_1_out_13), .Out_14(memory_1_out_14), .Out_15(memory_1_out_15), .Out_16(memory_1_out_16),
    .Out_17(memory_1_out_17), .Out_18(memory_1_out_18), .Out_19(memory_1_out_19), .Out_20(memory_1_out_20),
    .Out_21(memory_1_out_21), .Out_22(memory_1_out_22), .Out_23(memory_1_out_23), .Out_24(memory_1_out_24),
    .Out_25(memory_1_out_25), .Out_26(memory_1_out_26), .Out_27(memory_1_out_27), .Out_28(memory_1_out_28),
    .Out_29(memory_1_out_29), .Out_30(memory_1_out_30), .Out_31(memory_1_out_31), .Out_32(memory_1_out_32),
    .Out_33(memory_1_out_33), .Out_34(memory_1_out_34), .Out_35(memory_1_out_35), .Out_36(memory_1_out_36),
    .Out_37(memory_1_out_37), .Out_38(memory_1_out_38), .Out_39(memory_1_out_39), .Out_40(memory_1_out_40),
    .Out_41(memory_1_out_41), .Out_42(memory_1_out_42), .Out_43(memory_1_out_43), .Out_44(memory_1_out_44),
    .Out_45(memory_1_out_45), .Out_46(memory_1_out_46), .Out_47(memory_1_out_47), .Out_48(memory_1_out_48),
    .Out_49(memory_1_out_49), .Out_50(memory_1_out_50), .Out_51(memory_1_out_51), .Out_52(memory_1_out_52),
    .Out_53(memory_1_out_53), .Out_54(memory_1_out_54), .Out_55(memory_1_out_55), .Out_56(memory_1_out_56),
    .Out_57(memory_1_out_57), .Out_58(memory_1_out_58), .Out_59(memory_1_out_59), .Out_60(memory_1_out_60),
    .Out_61(memory_1_out_61), .Out_62(memory_1_out_62), .Out_63(memory_1_out_63), .Out_64(memory_1_out_64));
  not not_1 (not_1_out, Con_1[5]);
  or or_1 (or_1_out, Pinout[3], Pinout[2], Pinout[1], Pinout[0], p);
  LED Border (.in(Pinout[5]));
  Button button (.out(Pinout[3]));
  Button button_2 (.out(Pinout[2]));
  Demultiplexer #(.select(5), .width(32), .disabled(0)) demultiplexer_1 (
    .in(LY), .sel(Con_1[4:0]), .en(not_1_out));  // open: out0, out1, out2, out3, out4, out5, out6, out7, out8, out9, out10, out11, out12, out13, out14, out15, out16, out17, out18, out19, out20, out21, out22, out23, out24, out25, out26, out27, out28, out29, out30, out31
  assign XL1 = buffer_64_out;  // Buffer buffer_2, 32 bits wide
  buf buffer_3 (buffer_64_out[29], buffer_8_out[2]);
  buf buffer_4 (buffer_64_out[28], buffer_8_out[3]);
  buf buffer_5 (buffer_64_out[27], buffer_8_out[4]);
  buf buffer_6 (buffer_64_out[31], buffer_8_out[0]);
  buf buffer_7 (buffer_64_out[30], buffer_8_out[1]);
  assign buffer_8_out = X1;  // Buffer buffer_8, 32 bits wide
  assign XL2 = buffer_69_out;  // Buffer buffer_9, 32 bits wide
  buf buffer_10 (buffer_69_out[27], buffer_15_out[4]);
  buf buffer_11 (buffer_69_out[31], buffer_15_out[0]);
  buf buffer_12 (buffer_69_out[29], buffer_15_out[2]);
  buf buffer_13 (buffer_69_out[28], buffer_15_out[3]);
  buf buffer_14 (buffer_69_out[30], buffer_15_out[1]);
  assign buffer_15_out = X2;  // Buffer buffer_15, 32 bits wide
  Button Force_Print (.out(p));
  Button Reset (.out(Res));
  buf buffer_16 (buffer_64_out[23], buffer_8_out[8]);
  buf buffer_17 (buffer_64_out[24], buffer_8_out[7]);
  buf buffer_18 (buffer_64_out[26], buffer_8_out[5]);
  buf buffer_19 (buffer_64_out[25], buffer_8_out[6]);
  buf buffer_20 (buffer_64_out[22], buffer_8_out[9]);
  buf buffer_21 (buffer_64_out[20], buffer_8_out[11]);
  buf buffer_22 (buffer_64_out[19], buffer_8_out[12]);
  buf buffer_23 (buffer_64_out[21], buffer_8_out[10]);
  buf buffer_24 (buffer_69_out[20], buffer_15_out[11]);
  buf buffer_25 (buffer_69_out[26], buffer_15_out[5]);
  buf buffer_26 (buffer_69_out[24], buffer_15_out[7]);
  buf buffer_27 (buffer_69_out[25], buffer_15_out[6]);
  buf buffer_28 (buffer_69_out[19], buffer_15_out[12]);
  buf buffer_29 (buffer_69_out[23], buffer_15_out[8]);
  buf buffer_30 (buffer_69_out[22], buffer_15_out[9]);
  buf buffer_31 (buffer_69_out[21], buffer_15_out[10]);
  DotMatrix #(.matrixcols(32), .matrixrows(1)) dotmatrix_4 (
    .col0(X2[31]), .col1(X2[30]), .col2(X2[29]), .col3(X2[28]), .col4(X2[27]), .col5(X2[26]), .col6(X2[25]),
    .col7(X2[24]), .col8(X2[23]), .col9(X2[22]), .col10(X2[21]), .col11(X2[20]), .col12(X2[19]),
    .col13(X2[18]), .col14(X2[17]), .col15(X2[16]), .col16(X2[15]), .col17(X2[14]), .col18(X2[13]),
    .col19(X2[12]), .col20(X2[11]), .col21(X2[10]), .col22(X2[9]), .col23(X2[8]), .col24(X2[7]),
    .col25(X2[6]), .col26(X2[5]), .col27(X2[4]), .col28(X2[3]), .col29(X2[2]), .col30(X2[1]), .col31(X2[0]));
  DotMatrix #(.matrixcols(32), .matrixrows(32)) dotmatrix_5 (
    .col0(memory_1_out_33), .col1(memory_1_out_34), .col2(memory_1_out_35), .col3(memory_1_out_36),
    .col4(memory_1_out_37), .col5(memory_1_out_38), .col6(memory_1_out_39), .col7(memory_1_out_40),
    .col8(memory_1_out_41), .col9(memory_1_out_42), .col10(memory_1_out_43), .col11(memory_1_out_44),
    .col12(memory_1_out_45), .col13(memory_1_out_46), .col14(memory_1_out_47), .col15(memory_1_out_48),
    .col16(memory_1_out_49), .col17(memory_1_out_50), .col18(memory_1_out_51), .col19(memory_1_out_52),
    .col20(memory_1_out_53), .col21(memory_1_out_54), .col22(memory_1_out_55), .col23(memory_1_out_56),
    .col24(memory_1_out_57), .col25(memory_1_out_58), .col26(memory_1_out_59), .col27(memory_1_out_60),
    .col28(memory_1_out_61), .col29(memory_1_out_62), .col30(memory_1_out_63), .col31(memory_1_out_64));
  not not_2 (not_2_out, Con_2[5]);
  buf buffer_32 (buffer_64_out[18], buffer_8_out[13]);
  buf buffer_33 (buffer_64_out[17], buffer_8_out[14]);
  buf buffer_34 (buffer_64_out[16], buffer_8_out[15]);
  buf buffer_35 (buffer_64_out[13], buffer_8_out[18]);
  buf buffer_36 (buffer_64_out[14], buffer_8_out[17]);
  buf buffer_37 (buffer_64_out[12], buffer_8_out[19]);
  buf buffer_38 (buffer_64_out[15], buffer_8_out[16]);
  buf buffer_39 (buffer_64_out[11], buffer_8_out[20]);
  buf buffer_40 (buffer_69_out[12], buffer_15_out[19]);
  buf buffer_41 (buffer_69_out[16], buffer_15_out[15]);
  buf buffer_42 (buffer_69_out[14], buffer_15_out[17]);
  buf buffer_43 (buffer_69_out[11], buffer_15_out[20]);
  buf buffer_44 (buffer_69_out[17], buffer_15_out[14]);
  buf buffer_45 (buffer_69_out[18], buffer_15_out[13]);
  buf buffer_46 (buffer_69_out[15], buffer_15_out[16]);
  buf buffer_47 (buffer_69_out[13], buffer_15_out[18]);
  buf buffer_48 (buffer_64_out[3], buffer_8_out[28]);
  buf buffer_49 (buffer_64_out[4], buffer_8_out[27]);
  buf buffer_50 (buffer_64_out[8], buffer_8_out[23]);
  buf buffer_51 (buffer_64_out[10], buffer_8_out[21]);
  buf buffer_52 (buffer_64_out[9], buffer_8_out[22]);
  buf buffer_53 (buffer_64_out[5], buffer_8_out[26]);
  buf buffer_54 (buffer_64_out[6], buffer_8_out[25]);
  buf buffer_55 (buffer_64_out[7], buffer_8_out[24]);
  buf buffer_56 (buffer_69_out[10], buffer_15_out[21]);
  buf buffer_57 (buffer_69_out[7], buffer_15_out[24]);
  buf buffer_58 (buffer_69_out[9], buffer_15_out[22]);
  buf buffer_59 (buffer_69_out[4], buffer_15_out[27]);
  buf buffer_60 (buffer_69_out[3], buffer_15_out[28]);
  buf buffer_61 (buffer_69_out[5], buffer_15_out[26]);
  buf buffer_62 (buffer_69_out[6], buffer_15_out[25]);
  buf buffer_63 (buffer_69_out[8], buffer_15_out[23]);
  Button button_3 (.out(Pinout[1]));
  LED Border_2 (.in(Pinout[4]));
  Button v (.out(Pinout[0]));
  Demultiplexer #(.select(5), .width(32), .disabled(0)) demultiplexer_2 (
    .in(LY), .sel(Con_2[4:0]), .en(not_2_out));  // open: out0, out1, out2, out3, out4, out5, out6, out7, out8, out9, out10, out11, out12, out13, out14, out15, out16, out17, out18, out19, out20, out21, out22, out23, out24, out25, out26, out27, out28, out29, out30, out31
  buf buffer_64 (buffer_64_out[0], buffer_8_out[31]);
  buf buffer_65 (buffer_64_out[2], buffer_8_out[29]);
  buf buffer_66 (buffer_64_out[1], buffer_8_out[30]);
  buf buffer_67 (buffer_69_out[1], buffer_15_out[30]);
  buf buffer_68 (buffer_69_out[2], buffer_15_out[29]);
  buf buffer_69 (buffer_69_out[0], buffer_15_out[31]);
  counter counter_1 (
    .Double(1'b0), .Count_5(C5), .Led(Pinout[4]), .Lower_Button(Pinout[1]), .Raise_Button(Pinout[0]));  // open: Count_6
  vertCtrl vertctrl_1 (.Count(C5), .Out(LY));
  assign X1 = horizctrl_1_out1_2;  // Buffer buffer_70, 32 bits wide
  horizCtrl horizctrl_1 (
    .Count(counter_2_count_6), .Out1(X2), .Out1_2(horizctrl_1_out1_2), .Con_1(Con_1), .Con_2(Con_2));
  counter counter_2 (
    .Double(1'b1), .Count_6(counter_2_count_6), .Led(Pinout[5]), .Lower_Button(Pinout[3]),
    .Raise_Button(Pinout[2]));  // open: Count_5

  // Other names for the same wires on the sheet: Y[31:0] = LY
endmodule

module horizCtrl (
  input  [5:0] Count,
  output [5:0] Con_2,
  output [5:0] Con_1,
  output [31:0] Out1,
  output [31:0] Out1_2
);

  wire not_1_out, not_2_out, not_3_out, not_4_out, not_5_out;
  wire [4:0] buffer_1_out, buffer_6_out, controlled_buffer_5_out, controlled_buffer_6_out;
  wire [5:0] bit_extender_1_out, bit_extender_2_out;
  wire [31:0] demultiplexer_1_out31, demultiplexer_2_out31;

  assign Con_2 = not_2_out ? 6'b100000 : 6'bz;  // Controlled_Buffer controlled_buffer_1
  assign Con_2 = not_3_out ? bit_extender_1_out : 6'bz;  // Controlled_Buffer controlled_buffer_2
  assign bit_extender_1_out = {{1{1'b0}}, buffer_6_out};  // Bit_Extender bit_extender_1
  assign Con_1 = not_3_out ? 6'b100000 : 6'bz;  // Controlled_Buffer controlled_buffer_3
  assign bit_extender_2_out = {{1{1'b0}}, buffer_1_out};  // Bit_Extender bit_extender_2
  assign Con_1 = not_1_out ? bit_extender_2_out : 6'bz;  // Controlled_Buffer controlled_buffer_4
  assign controlled_buffer_5_out = not_1_out ? buffer_1_out : 5'bz;  // Controlled_Buffer controlled_buffer_5
  buf buffer_1 (buffer_1_out[0], Count[0]);
  buf buffer_2 (buffer_1_out[1], Count[1]);
  buf buffer_3 (buffer_1_out[2], Count[2]);
  not not_1 (not_1_out, Count[5]);
  buf buffer_4 (buffer_1_out[3], Count[3]);
  buf buffer_5 (buffer_1_out[4], Count[4]);
  buf buffer_6 (buffer_6_out[0], Count[0]);
  buf buffer_7 (buffer_6_out[1], Count[1]);
  buf buffer_8 (buffer_6_out[2], Count[2]);
  buf buffer_9 (buffer_6_out[3], Count[3]);
  buf buffer_10 (buffer_6_out[4], Count[4]);
  assign controlled_buffer_6_out = Count[5] ? buffer_6_out : 5'bz;  // Controlled_Buffer controlled_buffer_6
  assign Out1_2 = not_1_out ? demultiplexer_1_out31 : 32'bz;  // Controlled_Buffer controlled_buffer_7
  assign Out1_2 = Count[5] ? {32{1'b0}} : 32'bz;  // Controlled_Buffer controlled_buffer_8
  not not_2 (not_2_out, not_3_out);
  not not_3 (not_3_out, not_1_out);
  Demultiplexer #(.select(5)) demultiplexer_1 (
    .out0(demultiplexer_1_out31[31]), .out1(demultiplexer_1_out31[30]), .out2(demultiplexer_1_out31[29]),
    .out3(demultiplexer_1_out31[28]), .out4(demultiplexer_1_out31[27]), .out5(demultiplexer_1_out31[26]),
    .out6(demultiplexer_1_out31[25]), .out7(demultiplexer_1_out31[24]), .out8(demultiplexer_1_out31[23]),
    .out9(demultiplexer_1_out31[22]), .out10(demultiplexer_1_out31[21]), .out11(demultiplexer_1_out31[20]),
    .out12(demultiplexer_1_out31[19]), .out13(demultiplexer_1_out31[18]), .out14(demultiplexer_1_out31[17]),
    .out15(demultiplexer_1_out31[16]), .out16(demultiplexer_1_out31[15]), .out17(demultiplexer_1_out31[14]),
    .out18(demultiplexer_1_out31[13]), .out19(demultiplexer_1_out31[12]), .out20(demultiplexer_1_out31[11]),
    .out21(demultiplexer_1_out31[10]), .out22(demultiplexer_1_out31[9]), .out23(demultiplexer_1_out31[8]),
    .out24(demultiplexer_1_out31[7]), .out25(demultiplexer_1_out31[6]), .out26(demultiplexer_1_out31[5]),
    .out27(demultiplexer_1_out31[4]), .out28(demultiplexer_1_out31[3]), .out29(demultiplexer_1_out31[2]),
    .out30(demultiplexer_1_out31[1]), .out31(demultiplexer_1_out31[0]), .in(1'b1),
    .sel(controlled_buffer_5_out));  // open: en
  not not_4 (not_4_out, Count[5]);
  Demultiplexer #(.select(5)) demultiplexer_2 (
    .out0(demultiplexer_2_out31[31]), .out1(demultiplexer_2_out31[30]), .out2(demultiplexer_2_out31[29]),
    .out3(demultiplexer_2_out31[28]), .out4(demultiplexer_2_out31[27]), .out5(demultiplexer_2_out31[26]),
    .out6(demultiplexer_2_out31[25]), .out7(demultiplexer_2_out31[24]), .out8(demultiplexer_2_out31[23]),
    .out9(demultiplexer_2_out31[22]), .out10(demultiplexer_2_out31[21]), .out11(demultiplexer_2_out31[20]),
    .out12(demultiplexer_2_out31[19]), .out13(demultiplexer_2_out31[18]), .out14(demultiplexer_2_out31[17]),
    .out15(demultiplexer_2_out31[16]), .out16(demultiplexer_2_out31[15]), .out17(demultiplexer_2_out31[14]),
    .out18(demultiplexer_2_out31[13]), .out19(demultiplexer_2_out31[12]), .out20(demultiplexer_2_out31[11]),
    .out21(demultiplexer_2_out31[10]), .out22(demultiplexer_2_out31[9]), .out23(demultiplexer_2_out31[8]),
    .out24(demultiplexer_2_out31[7]), .out25(demultiplexer_2_out31[6]), .out26(demultiplexer_2_out31[5]),
    .out27(demultiplexer_2_out31[4]), .out28(demultiplexer_2_out31[3]), .out29(demultiplexer_2_out31[2]),
    .out30(demultiplexer_2_out31[1]), .out31(demultiplexer_2_out31[0]), .in(1'b1),
    .sel(controlled_buffer_6_out));  // open: en
  assign Out1 = not_5_out ? demultiplexer_2_out31 : 32'bz;  // Controlled_Buffer controlled_buffer_9
  assign Out1 = not_4_out ? {32{1'b0}} : 32'bz;  // Controlled_Buffer controlled_buffer_10
  not not_5 (not_5_out, not_4_out);
endmodule

module vertCtrl (
  input  [4:0] Count,
  output [31:0] Out
);

  wire [4:0] buffer_1_out;

  buf buffer_1 (buffer_1_out[0], Count[0]);
  buf buffer_2 (buffer_1_out[1], Count[1]);
  buf buffer_3 (buffer_1_out[2], Count[2]);
  buf buffer_4 (buffer_1_out[3], Count[3]);
  buf buffer_5 (buffer_1_out[4], Count[4]);
  Demultiplexer #(.select(5)) demultiplexer_1 (
    .out0(Out[31]), .out1(Out[30]), .out2(Out[29]), .out3(Out[28]), .out4(Out[27]), .out5(Out[26]),
    .out6(Out[25]), .out7(Out[24]), .out8(Out[23]), .out9(Out[22]), .out10(Out[21]), .out11(Out[20]),
    .out12(Out[19]), .out13(Out[18]), .out14(Out[17]), .out15(Out[16]), .out16(Out[15]), .out17(Out[14]),
    .out18(Out[13]), .out19(Out[12]), .out20(Out[11]), .out21(Out[10]), .out22(Out[9]), .out23(Out[8]),
    .out24(Out[7]), .out25(Out[6]), .out26(Out[5]), .out27(Out[4]), .out28(Out[3]), .out29(Out[2]),
    .out30(Out[1]), .out31(Out[0]), .in(1'b1), .sel(buffer_1_out));  // open: en
endmodule

module counter (
  input  Double,
  input  Lower_Button,
  input  Raise_Button,
  output [4:0] Count_5,
  output [5:0] Count_6,
  output Led
);

  wire and_1_out, and_2_out, ap, counter_1_carry, counter_2_carry, ndbl;

  not not_1 (ndbl, Double);
  Counter #(.width(5), .max('h1f), .ongoal("stay")) counter_1 (
    .load(Lower_Button), .count(ap), .Q(Count_5), .carry(counter_1_carry), .clk(ap));  // open: D, clr
  Counter #(.width(6), .max('h3f), .ongoal("stay")) counter_2 (
    .load(Lower_Button), .count(ap), .Q(Count_6), .carry(counter_2_carry), .clk(ap));  // open: D, clr
  and and_1 (and_1_out, counter_2_carry, Double);
  or or_1 (ap, Raise_Button, Lower_Button);
  and and_2 (and_2_out, counter_1_carry, ndbl);
  assign ap = Lower_Button ? Lower_Button : 1'bz;  // Controlled_Buffer controlled_buffer_1
  assign ap = Raise_Button ? Raise_Button : 1'bz;  // Controlled_Buffer controlled_buffer_2
  or or_2 (Led, and_2_out, and_1_out);

  // Other names for the same wires on the sheet: dbl = Double; lwr = Lower_Button
endmodule

module Memory (
  input  Clock,
  input  Reset,
  input  [31:0] X_Location_1,
  input  [31:0] X_Location_2,
  input  [31:0] Y_Location,
  output [31:0] Out_1,
  output [31:0] Out_2,
  output [31:0] Out_3,
  output [31:0] Out_4,
  output [31:0] Out_5,
  output [31:0] Out_6,
  output [31:0] Out_7,
  output [31:0] Out_8,
  output [31:0] Out_9,
  output [31:0] Out_10,
  output [31:0] Out_11,
  output [31:0] Out_12,
  output [31:0] Out_13,
  output [31:0] Out_14,
  output [31:0] Out_15,
  output [31:0] Out_16,
  output [31:0] Out_17,
  output [31:0] Out_18,
  output [31:0] Out_19,
  output [31:0] Out_20,
  output [31:0] Out_21,
  output [31:0] Out_22,
  output [31:0] Out_23,
  output [31:0] Out_24,
  output [31:0] Out_25,
  output [31:0] Out_26,
  output [31:0] Out_27,
  output [31:0] Out_28,
  output [31:0] Out_29,
  output [31:0] Out_30,
  output [31:0] Out_31,
  output [31:0] Out_32,
  output [31:0] Out_33,
  output [31:0] Out_34,
  output [31:0] Out_35,
  output [31:0] Out_36,
  output [31:0] Out_37,
  output [31:0] Out_38,
  output [31:0] Out_39,
  output [31:0] Out_40,
  output [31:0] Out_41,
  output [31:0] Out_42,
  output [31:0] Out_43,
  output [31:0] Out_44,
  output [31:0] Out_45,
  output [31:0] Out_46,
  output [31:0] Out_47,
  output [31:0] Out_48,
  output [31:0] Out_49,
  output [31:0] Out_50,
  output [31:0] Out_51,
  output [31:0] Out_52,
  output [31:0] Out_53,
  output [31:0] Out_54,
  output [31:0] Out_55,
  output [31:0] Out_56,
  output [31:0] Out_57,
  output [31:0] Out_58,
  output [31:0] Out_59,
  output [31:0] Out_60,
  output [31:0] Out_61,
  output [31:0] Out_62,
  output [31:0] Out_63,
  output [31:0] Out_64
);

  wire bitfinder_1_found, bitfinder_2_found, C, decoder_1_out0, decoder_1_out1, decoder_1_out2,
       decoder_1_out3, decoder_1_out4, decoder_1_out5, decoder_1_out6, decoder_1_out7, decoder_1_out8,
       decoder_1_out9, decoder_1_out10, decoder_1_out11, decoder_1_out12, decoder_1_out13, decoder_1_out14,
       decoder_1_out15, decoder_1_out16, decoder_1_out17, decoder_1_out18, decoder_1_out19, decoder_1_out20,
       decoder_1_out21, decoder_1_out22, decoder_1_out23, decoder_1_out24, decoder_1_out25, decoder_1_out26,
       decoder_1_out27, decoder_1_out28, decoder_1_out29, decoder_1_out30, decoder_1_out31, decoder_2_out0,
       decoder_2_out1, decoder_2_out2, decoder_2_out3, decoder_2_out4, decoder_2_out5, decoder_2_out6,
       decoder_2_out7, decoder_2_out8, decoder_2_out9, decoder_2_out10, decoder_2_out11, decoder_2_out12,
       decoder_2_out13, decoder_2_out14, decoder_2_out15, decoder_2_out16, decoder_2_out17, decoder_2_out18,
       decoder_2_out19, decoder_2_out20, decoder_2_out21, decoder_2_out22, decoder_2_out23, decoder_2_out24,
       decoder_2_out25, decoder_2_out26, decoder_2_out27, decoder_2_out28, decoder_2_out29, decoder_2_out30,
       decoder_2_out31, reg_1_out_button, reg_2_out_button, reg_3_out_button, reg_4_out_button,
       reg_5_out_button, reg_6_out_button, reg_7_out_button, reg_8_out_button, reg_9_out_button,
       reg_10_out_button, reg_11_out_button, reg_12_out_button, reg_13_out_button, reg_14_out_button,
       reg_15_out_button, reg_16_out_button, reg_17_out_button, reg_18_out_button, reg_19_out_button,
       reg_20_out_button, reg_21_out_button, reg_22_out_button, reg_23_out_button, reg_24_out_button,
       reg_25_out_button, reg_26_out_button, reg_27_out_button, reg_28_out_button, reg_29_out_button,
       reg_30_out_button, reg_31_out_button, reg_32_out_button, reg_33_out_button, reg_34_out_button,
       reg_35_out_button, reg_36_out_button, reg_37_out_button, reg_38_out_button, reg_39_out_button,
       reg_40_out_button, reg_41_out_button, reg_42_out_button, reg_43_out_button, reg_44_out_button,
       reg_45_out_button, reg_46_out_button, reg_47_out_button, reg_48_out_button, reg_49_out_button,
       reg_50_out_button, reg_51_out_button, reg_52_out_button, reg_53_out_button, reg_54_out_button,
       reg_55_out_button, reg_56_out_button, reg_57_out_button, reg_58_out_button, reg_59_out_button,
       reg_60_out_button, reg_61_out_button, reg_62_out_button, reg_63_out_button, reg_64_out_button,
       undriven, undriven_2, undriven_3, undriven_4, undriven_5, undriven_6, undriven_7, undriven_8,
       undriven_9, undriven_10, undriven_11, undriven_12, undriven_13, undriven_14, undriven_15, undriven_16,
       undriven_17, undriven_18, undriven_19, undriven_20, undriven_21, undriven_22, undriven_23,
       undriven_24, undriven_25, undriven_26, undriven_27, undriven_28, undriven_29, undriven_30,
       undriven_31, undriven_32, undriven_33, undriven_34, undriven_35, undriven_36, undriven_37,
       undriven_38, undriven_39, undriven_40, undriven_41, undriven_42, undriven_43, undriven_44,
       undriven_45, undriven_46, undriven_47, undriven_48, undriven_49, undriven_50, undriven_51,
       undriven_52, undriven_53, undriven_54, undriven_55, undriven_56, undriven_57, undriven_58,
       undriven_59, undriven_60, undriven_61, undriven_62, undriven_63, undriven_64;
  wire [4:0] bitfinder_1_index, bitfinder_2_index;
  wire [31:0] reg_1_out_input, reg_2_out_input, reg_3_out_input, reg_4_out_input, reg_5_out_input,
       reg_6_out_input, reg_7_out_input, reg_8_out_input, reg_9_out_input, reg_10_out_input,
       reg_11_out_input, reg_12_out_input, reg_13_out_input, reg_14_out_input, reg_15_out_input,
       reg_16_out_input, reg_17_out_input, reg_18_out_input, reg_19_out_input, reg_20_out_input,
       reg_21_out_input, reg_22_out_input, reg_23_out_input, reg_24_out_input, reg_25_out_input,
       reg_26_out_input, reg_27_out_input, reg_28_out_input, reg_29_out_input, reg_30_out_input,
       reg_31_out_input, reg_32_out_input, reg_33_out_input, reg_34_out_input, reg_35_out_input,
       reg_36_out_input, reg_37_out_input, reg_38_out_input, reg_39_out_input, reg_40_out_input,
       reg_41_out_input, reg_42_out_input, reg_43_out_input, reg_44_out_input, reg_45_out_input,
       reg_46_out_input, reg_47_out_input, reg_48_out_input, reg_49_out_input, reg_50_out_input,
       reg_51_out_input, reg_52_out_input, reg_53_out_input, reg_54_out_input, reg_55_out_input,
       reg_56_out_input, reg_57_out_input, reg_58_out_input, reg_59_out_input, reg_60_out_input,
       reg_61_out_input, reg_62_out_input, reg_63_out_input, reg_64_out_input;

  not not_1 (C, Clock);
  Decoder #(.select(5)) decoder_1 (
    .out0(decoder_1_out0), .out1(decoder_1_out1), .out2(decoder_1_out2), .out3(decoder_1_out3),
    .out4(decoder_1_out4), .out5(decoder_1_out5), .out6(decoder_1_out6), .out7(decoder_1_out7),
    .out8(decoder_1_out8), .out9(decoder_1_out9), .out10(decoder_1_out10), .out11(decoder_1_out11),
    .out12(decoder_1_out12), .out13(decoder_1_out13), .out14(decoder_1_out14), .out15(decoder_1_out15),
    .out16(decoder_1_out16), .out17(decoder_1_out17), .out18(decoder_1_out18), .out19(decoder_1_out19),
    .out20(decoder_1_out20), .out21(decoder_1_out21), .out22(decoder_1_out22), .out23(decoder_1_out23),
    .out24(decoder_1_out24), .out25(decoder_1_out25), .out26(decoder_1_out26), .out27(decoder_1_out27),
    .out28(decoder_1_out28), .out29(decoder_1_out29), .out30(decoder_1_out30), .out31(decoder_1_out31),
    .sel(bitfinder_1_index), .en(bitfinder_1_found));
  BitFinder #(.width(32)) bitfinder_1 (.in(X_Location_1), .index(bitfinder_1_index), .found(bitfinder_1_found));
  BitFinder #(.width(32)) bitfinder_2 (.in(X_Location_2), .index(bitfinder_2_index), .found(bitfinder_2_found));
  Decoder #(.select(5)) decoder_2 (
    .out0(decoder_2_out0), .out1(decoder_2_out1), .out2(decoder_2_out2), .out3(decoder_2_out3),
    .out4(decoder_2_out4), .out5(decoder_2_out5), .out6(decoder_2_out6), .out7(decoder_2_out7),
    .out8(decoder_2_out8), .out9(decoder_2_out9), .out10(decoder_2_out10), .out11(decoder_2_out11),
    .out12(decoder_2_out12), .out13(decoder_2_out13), .out14(decoder_2_out14), .out15(decoder_2_out15),
    .out16(decoder_2_out16), .out17(decoder_2_out17), .out18(decoder_2_out18), .out19(decoder_2_out19),
    .out20(decoder_2_out20), .out21(decoder_2_out21), .out22(decoder_2_out22), .out23(decoder_2_out23),
    .out24(decoder_2_out24), .out25(decoder_2_out25), .out26(decoder_2_out26), .out27(decoder_2_out27),
    .out28(decoder_2_out28), .out29(decoder_2_out29), .out30(decoder_2_out30), .out31(decoder_2_out31),
    .sel(bitfinder_2_index), .en(bitfinder_2_found));
  Reg reg_1 (
    .Enabled(decoder_1_out0), .Clear({Reset, undriven}), .Out_Button({C, reg_1_out_button}),
    .Input(Y_Location), .Output(Out_1), .Out_Input(reg_1_out_input));
  Reg reg_2 (
    .Enabled(decoder_1_out1), .Clear({undriven, undriven_2}),
    .Out_Button({reg_1_out_button, reg_2_out_button}), .Input(reg_1_out_input), .Output(Out_2),
    .Out_Input(reg_2_out_input));
  Reg reg_3 (
    .Enabled(decoder_1_out2), .Clear({undriven_2, undriven_3}),
    .Out_Button({reg_2_out_button, reg_3_out_button}), .Input(reg_2_out_input), .Output(Out_3),
    .Out_Input(reg_3_out_input));
  Reg reg_4 (
    .Enabled(decoder_1_out3), .Clear({undriven_3, undriven_4}),
    .Out_Button({reg_3_out_button, reg_4_out_button}), .Input(reg_3_out_input), .Output(Out_4),
    .Out_Input(reg_4_out_input));
  Reg reg_5 (
    .Enabled(decoder_1_out4), .Clear({undriven_4, undriven_5}),
    .Out_Button({reg_4_out_button, reg_5_out_button}), .Input(reg_4_out_input), .Output(Out_5),
    .Out_Input(reg_5_out_input));
  Reg reg_6 (
    .Enabled(decoder_1_out5), .Clear({undriven_5, undriven_6}),
    .Out_Button({reg_5_out_button, reg_6_out_button}), .Input(reg_5_out_input), .Output(Out_6),
    .Out_Input(reg_6_out_input));
  Reg reg_7 (
    .Enabled(decoder_1_out6), .Clear({undriven_6, undriven_7}),
    .Out_Button({reg_6_out_button, reg_7_out_button}), .Input(reg_6_out_input), .Output(Out_7),
    .Out_Input(reg_7_out_input));
  Reg reg_8 (
    .Enabled(decoder_1_out7), .Clear({undriven_7, undriven_8}),
    .Out_Button({reg_7_out_button, reg_8_out_button}), .Input(reg_7_out_input), .Output(Out_8),
    .Out_Input(reg_8_out_input));
  Reg reg_9 (
    .Enabled(decoder_1_out8), .Clear({undriven_8, undriven_9}),
    .Out_Button({reg_8_out_button, reg_9_out_button}), .Input(reg_8_out_input), .Output(Out_9),
    .Out_Input(reg_9_out_input));
  Reg reg_10 (
    .Enabled(decoder_1_out9), .Clear({undriven_9, undriven_10}),
    .Out_Button({reg_9_out_button, reg_10_out_button}), .Input(reg_9_out_input), .Output(Out_10),
    .Out_Input(reg_10_out_input));
  Reg reg_11 (
    .Enabled(decoder_1_out10), .Clear({undriven_10, undriven_11}),
    .Out_Button({reg_10_out_button, reg_11_out_button}), .Input(reg_10_out_input), .Output(Out_11),
    .Out_Input(reg_11_out_input));
  Reg reg_12 (
    .Enabled(decoder_1_out11), .Clear({undriven_11, undriven_12}),
    .Out_Button({reg_11_out_button, reg_12_out_button}), .Input(reg_11_out_input), .Output(Out_12),
    .Out_Input(reg_12_out_input));
  Reg reg_13 (
    .Enabled(decoder_1_out12), .Clear({undriven_12, undriven_13}),
    .Out_Button({reg_12_out_button, reg_13_out_button}), .Input(reg_12_out_input), .Output(Out_13),
    .Out_Input(reg_13_out_input));
  Reg reg_14 (
    .Enabled(decoder_1_out13), .Clear({undriven_13, undriven_14}),
    .Out_Button({reg_13_out_button, reg_14_out_button}), .Input(reg_13_out_input), .Output(Out_14),
    .Out_Input(reg_14_out_input));
  Reg reg_15 (
    .Enabled(decoder_1_out14), .Clear({undriven_14, undriven_15}),
    .Out_Button({reg_14_out_button, reg_15_out_button}), .Input(reg_14_out_input), .Output(Out_15),
    .Out_Input(reg_15_out_input));
  Reg reg_16 (
    .Enabled(decoder_1_out15), .Clear({undriven_15, undriven_16}),
    .Out_Button({reg_15_out_button, reg_16_out_button}), .Input(reg_15_out_input), .Output(Out_16),
    .Out_Input(reg_16_out_input));
  Reg reg_17 (
    .Enabled(decoder_1_out16), .Clear({undriven_16, undriven_17}),
    .Out_Button({reg_16_out_button, reg_17_out_button}), .Input(reg_16_out_input), .Output(Out_17),
    .Out_Input(reg_17_out_input));
  Reg reg_18 (
    .Enabled(decoder_1_out17), .Clear({undriven_17, undriven_18}),
    .Out_Button({reg_17_out_button, reg_18_out_button}), .Input(reg_17_out_input), .Output(Out_18),
    .Out_Input(reg_18_out_input));
  Reg reg_19 (
    .Enabled(decoder_1_out18), .Clear({undriven_18, undriven_19}),
    .Out_Button({reg_18_out_button, reg_19_out_button}), .Input(reg_18_out_input), .Output(Out_19),
    .Out_Input(reg_19_out_input));
  Reg reg_20 (
    .Enabled(decoder_1_out19), .Clear({undriven_19, undriven_20}),
    .Out_Button({reg_19_out_button, reg_20_out_button}), .Input(reg_19_out_input), .Output(Out_20),
    .Out_Input(reg_20_out_input));
  Reg reg_21 (
    .Enabled(decoder_1_out20), .Clear({undriven_20, undriven_21}),
    .Out_Button({reg_20_out_button, reg_21_out_button}), .Input(reg_20_out_input), .Output(Out_21),
    .Out_Input(reg_21_out_input));
  Reg reg_22 (
    .Enabled(decoder_1_out21), .Clear({undriven_21, undriven_22}),
    .Out_Button({reg_21_out_button, reg_22_out_button}), .Input(reg_21_out_input), .Output(Out_22),
    .Out_Input(reg_22_out_input));
  Reg reg_23 (
    .Enabled(decoder_1_out22), .Clear({undriven_22, undriven_23}),
    .Out_Button({reg_22_out_button, reg_23_out_button}), .Input(reg_22_out_input), .Output(Out_23),
    .Out_Input(reg_23_out_input));
  Reg reg_24 (
    .Enabled(decoder_1_out23), .Clear({undriven_23, undriven_24}),
    .Out_Button({reg_23_out_button, reg_24_out_button}), .Input(reg_23_out_input), .Output(Out_24),
    .Out_Input(reg_24_out_input));
  Reg reg_25 (
    .Enabled(decoder_1_out24), .Clear({undriven_24, undriven_25}),
    .Out_Button({reg_24_out_button, reg_25_out_button}), .Input(reg_24_out_input), .Output(Out_25),
    .Out_Input(reg_25_out_input));
  Reg reg_26 (
    .Enabled(decoder_1_out25), .Clear({undriven_25, undriven_26}),
    .Out_Button({reg_25_out_button, reg_26_out_button}), .Input(reg_25_out_input), .Output(Out_26),
    .Out_Input(reg_26_out_input));
  Reg reg_27 (
    .Enabled(decoder_1_out26), .Clear({undriven_26, undriven_27}),
    .Out_Button({reg_26_out_button, reg_27_out_button}), .Input(reg_26_out_input), .Output(Out_27),
    .Out_Input(reg_27_out_input));
  Reg reg_28 (
    .Enabled(decoder_1_out27), .Clear({undriven_27, undriven_28}),
    .Out_Button({reg_27_out_button, reg_28_out_button}), .Input(reg_27_out_input), .Output(Out_28),
    .Out_Input(reg_28_out_input));
  Reg reg_29 (
    .Enabled(decoder_1_out28), .Clear({undriven_28, undriven_29}),
    .Out_Button({reg_28_out_button, reg_29_out_button}), .Input(reg_28_out_input), .Output(Out_29),
    .Out_Input(reg_29_out_input));
  Reg reg_30 (
    .Enabled(decoder_1_out29), .Clear({undriven_29, undriven_30}),
    .Out_Button({reg_29_out_button, reg_30_out_button}), .Input(reg_29_out_input), .Output(Out_30),
    .Out_Input(reg_30_out_input));
  Reg reg_31 (
    .Enabled(decoder_1_out30), .Clear({undriven_30, undriven_31}),
    .Out_Button({reg_30_out_button, reg_31_out_button}), .Input(reg_30_out_input), .Output(Out_31),
    .Out_Input(reg_31_out_input));
  Reg reg_32 (
    .Enabled(decoder_1_out31), .Clear({undriven_31, undriven_32}),
    .Out_Button({reg_31_out_button, reg_32_out_button}), .Input(reg_31_out_input), .Output(Out_32),
    .Out_Input(reg_32_out_input));
  Reg reg_33 (
    .Enabled(decoder_2_out0), .Clear({undriven_32, undriven_33}),
    .Out_Button({reg_32_out_button, reg_33_out_button}), .Input(reg_32_out_input), .Output(Out_33),
    .Out_Input(reg_33_out_input));
  Reg reg_34 (
    .Enabled(decoder_2_out1), .Clear({undriven_33, undriven_34}),
    .Out_Button({reg_33_out_button, reg_34_out_button}), .Input(reg_33_out_input), .Output(Out_34),
    .Out_Input(reg_34_out_input));
  Reg reg_35 (
    .Enabled(decoder_2_out2), .Clear({undriven_34, undriven_35}),
    .Out_Button({reg_34_out_button, reg_35_out_button}), .Input(reg_34_out_input), .Output(Out_35),
    .Out_Input(reg_35_out_input));
  Reg reg_36 (
    .Enabled(decoder_2_out3), .Clear({undriven_35, undriven_36}),
    .Out_Button({reg_35_out_button, reg_36_out_button}), .Input(reg_35_out_input), .Output(Out_36),
    .Out_Input(reg_36_out_input));
  Reg reg_37 (
    .Enabled(decoder_2_out4), .Clear({undriven_36, undriven_37}),
    .Out_Button({reg_36_out_button, reg_37_out_button}), .Input(reg_36_out_input), .Output(Out_37),
    .Out_Input(reg_37_out_input));
  Reg reg_38 (
    .Enabled(decoder_2_out5), .Clear({undriven_37, undriven_38}),
    .Out_Button({reg_37_out_button, reg_38_out_button}), .Input(reg_37_out_input), .Output(Out_38),
    .Out_Input(reg_38_out_input));
  Reg reg_39 (
    .Enabled(decoder_2_out6), .Clear({undriven_38, undriven_39}),
    .Out_Button({reg_38_out_button, reg_39_out_button}), .Input(reg_38_out_input), .Output(Out_39),
    .Out_Input(reg_39_out_input));
  Reg reg_40 (
    .Enabled(decoder_2_out7), .Clear({undriven_39, undriven_40}),
    .Out_Button({reg_39_out_button, reg_40_out_button}), .Input(reg_39_out_input), .Output(Out_40),
    .Out_Input(reg_40_out_input));
  Reg reg_41 (
    .Enabled(decoder_2_out8), .Clear({undriven_40, undriven_41}),
    .Out_Button({reg_40_out_button, reg_41_out_button}), .Input(reg_40_out_input), .Output(Out_41),
    .Out_Input(reg_41_out_input));
  Reg reg_42 (
    .Enabled(decoder_2_out9), .Clear({undriven_41, undriven_42}),
    .Out_Button({reg_41_out_button, reg_42_out_button}), .Input(reg_41_out_input), .Output(Out_42),
    .Out_Input(reg_42_out_input));
  Reg reg_43 (
    .Enabled(decoder_2_out10), .Clear({undriven_42, undriven_43}),
    .Out_Button({reg_42_out_button, reg_43_out_button}), .Input(reg_42_out_input), .Output(Out_43),
    .Out_Input(reg_43_out_input));
  Reg reg_44 (
    .Enabled(decoder_2_out11), .Clear({undriven_43, undriven_44}),
    .Out_Button({reg_43_out_button, reg_44_out_button}), .Input(reg_43_out_input), .Output(Out_44),
    .Out_Input(reg_44_out_input));
  Reg reg_45 (
    .Enabled(decoder_2_out12), .Clear({undriven_44, undriven_45}),
    .Out_Button({reg_44_out_button, reg_45_out_button}), .Input(reg_44_out_input), .Output(Out_45),
    .Out_Input(reg_45_out_input));
  Reg reg_46 (
    .Enabled(decoder_2_out13), .Clear({undriven_45, undriven_46}),
    .Out_Button({reg_45_out_button, reg_46_out_button}), .Input(reg_45_out_input), .Output(Out_46),
    .Out_Input(reg_46_out_input));
  Reg reg_47 (
    .Enabled(decoder_2_out14), .Clear({undriven_46, undriven_47}),
    .Out_Button({reg_46_out_button, reg_47_out_button}), .Input(reg_46_out_input), .Output(Out_47),
    .Out_Input(reg_47_out_input));
  Reg reg_48 (
    .Enabled(decoder_2_out15), .Clear({undriven_47, undriven_48}),
    .Out_Button({reg_47_out_button, reg_48_out_button}), .Input(reg_47_out_input), .Output(Out_48),
    .Out_Input(reg_48_out_input));
  Reg reg_49 (
    .Enabled(decoder_2_out16), .Clear({undriven_48, undriven_49}),
    .Out_Button({reg_48_out_button, reg_49_out_button}), .Input(reg_48_out_input), .Output(Out_49),
    .Out_Input(reg_49_out_input));
  Reg reg_50 (
    .Enabled(decoder_2_out17), .Clear({undriven_49, undriven_50}),
    .Out_Button({reg_49_out_button, reg_50_out_button}), .Input(reg_49_out_input), .Output(Out_50),
    .Out_Input(reg_50_out_input));
  Reg reg_51 (
    .Enabled(decoder_2_out18), .Clear({undriven_50, undriven_51}),
    .Out_Button({reg_50_out_button, reg_51_out_button}), .Input(reg_50_out_input), .Output(Out_51),
    .Out_Input(reg_51_out_input));
  Reg reg_52 (
    .Enabled(decoder_2_out19), .Clear({undriven_51, undriven_52}),
    .Out_Button({reg_51_out_button, reg_52_out_button}), .Input(reg_51_out_input), .Output(Out_52),
    .Out_Input(reg_52_out_input));
  Reg reg_53 (
    .Enabled(decoder_2_out20), .Clear({undriven_52, undriven_53}),
    .Out_Button({reg_52_out_button, reg_53_out_button}), .Input(reg_52_out_input), .Output(Out_53),
    .Out_Input(reg_53_out_input));
  Reg reg_54 (
    .Enabled(decoder_2_out21), .Clear({undriven_53, undriven_54}),
    .Out_Button({reg_53_out_button, reg_54_out_button}), .Input(reg_53_out_input), .Output(Out_54),
    .Out_Input(reg_54_out_input));
  Reg reg_55 (
    .Enabled(decoder_2_out22), .Clear({undriven_54, undriven_55}),
    .Out_Button({reg_54_out_button, reg_55_out_button}), .Input(reg_54_out_input), .Output(Out_55),
    .Out_Input(reg_55_out_input));
  Reg reg_56 (
    .Enabled(decoder_2_out23), .Clear({undriven_55, undriven_56}),
    .Out_Button({reg_55_out_button, reg_56_out_button}), .Input(reg_55_out_input), .Output(Out_56),
    .Out_Input(reg_56_out_input));
  Reg reg_57 (
    .Enabled(decoder_2_out24), .Clear({undriven_56, undriven_57}),
    .Out_Button({reg_56_out_button, reg_57_out_button}), .Input(reg_56_out_input), .Output(Out_57),
    .Out_Input(reg_57_out_input));
  Reg reg_58 (
    .Enabled(decoder_2_out25), .Clear({undriven_57, undriven_58}),
    .Out_Button({reg_57_out_button, reg_58_out_button}), .Input(reg_57_out_input), .Output(Out_58),
    .Out_Input(reg_58_out_input));
  Reg reg_59 (
    .Enabled(decoder_2_out26), .Clear({undriven_58, undriven_59}),
    .Out_Button({reg_58_out_button, reg_59_out_button}), .Input(reg_58_out_input), .Output(Out_59),
    .Out_Input(reg_59_out_input));
  Reg reg_60 (
    .Enabled(decoder_2_out27), .Clear({undriven_59, undriven_60}),
    .Out_Button({reg_59_out_button, reg_60_out_button}), .Input(reg_59_out_input), .Output(Out_60),
    .Out_Input(reg_60_out_input));
  Reg reg_61 (
    .Enabled(decoder_2_out28), .Clear({undriven_60, undriven_61}),
    .Out_Button({reg_60_out_button, reg_61_out_button}), .Input(reg_60_out_input), .Output(Out_61),
    .Out_Input(reg_61_out_input));
  Reg reg_62 (
    .Enabled(decoder_2_out29), .Clear({undriven_61, undriven_62}),
    .Out_Button({reg_61_out_button, reg_62_out_button}), .Input(reg_61_out_input), .Output(Out_62),
    .Out_Input(reg_62_out_input));
  Reg reg_63 (
    .Enabled(decoder_2_out30), .Clear({undriven_62, undriven_63}),
    .Out_Button({reg_62_out_button, reg_63_out_button}), .Input(reg_62_out_input), .Output(Out_63),
    .Out_Input(reg_63_out_input));
  Reg reg_64 (
    .Enabled(decoder_2_out31), .Clear({undriven_63, undriven_64}),
    .Out_Button({reg_63_out_button, reg_64_out_button}), .Input(reg_63_out_input), .Output(Out_64),
    .Out_Input(reg_64_out_input));
  // Probe on reg_64_out_input
  // Probe on reg_64_out_button
  // Probe on undriven_64

  // Other names for the same wires on the sheet: R = Reset; Y[31:0] = Y_Location
endmodule

module Reg (
  input  Enabled,
  input  Clear,
  input  Button,
  input  [31:0] Input,
  output [31:0] Output,
  output Out_Clear,
  output Out_Button,
  output [31:0] Out_Input
);

  wire and_1_out, bitselector_1_out, controlled_buffer_3_out, not_1_out, or_1_out;
  wire [4:0] bitfinder_1_index;
  wire [31:0] adder_1_out, controlled_buffer_1_out, controlled_buffer_4_out, controlled_buffer_5_out,
       controlled_buffer_6_out;

  assign controlled_buffer_1_out = Clear ? Input : 32'bz;  // Controlled_Buffer controlled_buffer_1
  and and_1 (and_1_out, ~Clear, Enabled);  // AND_Gate
  assign controlled_buffer_1_out = and_1_out ? adder_1_out : 32'bz;  // Controlled_Buffer controlled_buffer_2
  Register #(.width(32)) register_1 (.D(controlled_buffer_1_out), .Q(Output), .clk(or_1_out), .clr(Clear));  // open: en
  or or_1 (or_1_out, controlled_buffer_3_out, Clear);
  assign controlled_buffer_3_out = Enabled ? Button : 1'bz;  // Controlled_Buffer controlled_buffer_3
  assign controlled_buffer_4_out = not_1_out ? Output : 32'bz;  // Controlled_Buffer controlled_buffer_4
  not not_1 (not_1_out, bitselector_1_out);
  BitSelector #(.width(32)) bitselector_1 (.in(Output), .out(bitselector_1_out), .sel(bitfinder_1_index));
  assign controlled_buffer_5_out = not_1_out ? controlled_buffer_6_out : 32'bz;  // Controlled_Buffer controlled_buffer_5
  assign controlled_buffer_6_out = Enabled ? Input : 32'bz;  // Controlled_Buffer controlled_buffer_6
  BitFinder #(.width(32)) bitfinder_1 (.in(controlled_buffer_6_out), .index(bitfinder_1_index));  // open: found
  Adder #(.width(32)) adder_1 (
    .a(controlled_buffer_4_out), .b(controlled_buffer_5_out), .out(adder_1_out));  // open: cin, cout

  assign Out_Button = Button;
  assign Out_Clear = Clear;
  assign Out_Input = Input;
endmodule
